// Logisim project 8Bit_PC_V0.1.circ as structural Verilog: 16 circuits, main circuit main
module main (
);

  wire ABinv, ACin, alu_t_a1d61d21_1_zero, button_1_out, button_2_out, clk, clk_halt, DI, EEParg, EEPladr,
       flipflop_1_q, flipflop_2_q, IRI, NOT_AEO, NOT_EEPEO, NOT_EEwrite, NOT_PCEO, NOT_PCL, NOT_RAEO,
       NOT_RAMEO, NOT_RAMwrite, NOT_RBEO, PCCE, RAMladr, RLA, RLB;
  wire [7:0] eeprom_1_data, ireg_1_out, ireg_2_out, pc_1_debug_out, reg_ab_1_out_a, reg_ab_1_out_b;

  EEPROM eeprom_1 (
    .adr(eeprom_1_data), .NOT_write(NOT_EEwrite), .args(EEParg), .LoadAdr(EEPladr), .NOT_EO(NOT_EEPEO),
    .in(eeprom_1_data), .data(eeprom_1_data));
  Clock clock_1 (.ClkHalt(flipflop_1_q), .ClkMan(clk_halt), .Clk(clk));
  FlipFlop flipflop_1 (.toggle(button_1_out), .Q(flipflop_1_q));
  Button button_1 (.out(button_1_out));
  RAM ram_1 (
    .adr(eeprom_1_data), .NOT_EO(NOT_RAMEO), .NOT_write(NOT_RAMwrite), .LoadAdr(RAMladr),
    .Din(eeprom_1_data), .Dout(eeprom_1_data));
  IReg ireg_1 (.LE(IRI), .In(eeprom_1_data), .Out(ireg_1_out));
  // Probe on eeprom_1_data
  // Probe on eeprom_1_data
  ControllLogic controlllogic_1 (
    .Clk(clk), .IREG(ireg_1_out), .halt_man(flipflop_2_q), .zero(alu_t_a1d61d21_1_zero), .halt(clk_halt),
    .Disp_I(DI), .PC_LOAD_I(NOT_PCL), .RAM_ADR_I(RAMladr), .EEPROM_ADR_I(EEPladr), .REG_A_I(RLA),
    .REG_B_I(RLB), .REG_INST_I(IRI), .RAM_WRITE_I(NOT_RAMwrite), .EEPROM_WRITE_I(NOT_EEwrite),
    .PC_O(NOT_PCEO), .RAM_O(NOT_RAMEO), .EEPROM_O(NOT_EEPEO), .REG_A_O(NOT_RAEO), .REG_B_O(NOT_RBEO),
    .ALU_O(NOT_AEO), .PC_INC(PCCE), .ALU_Cin(ACin), .ALU_Binv(ABinv), .EEPROM_ARG(EEParg));  // open: out_20, out_21
  PC pc_1 (
    .LoadIn(eeprom_1_data), .PC_INC(PCCE), .Clk(clk), .NOT_load(NOT_PCL), .NOT_OE(NOT_PCEO),
    .Debug_Out(pc_1_debug_out), .PCout(eeprom_1_data));
  ALU_T_a1d61d21 alu_t_a1d61d21_1 (
    .Cin(ACin), .Binv(ABinv), .A(reg_ab_1_out_a), .B(reg_ab_1_out_b), .NOT_EO_36d354d6(NOT_AEO),
    .out(eeprom_1_data), .Zero(alu_t_a1d61d21_1_zero));
  Reg_AB reg_ab_1 (
    .LE_A(RLA), .LE_B(RLB), .In(eeprom_1_data), .NOT_EOA(NOT_RAEO), .NOT_OEB(NOT_RBEO), .A_E(eeprom_1_data),
    .Out_A(reg_ab_1_out_a), .B_E(eeprom_1_data), .Out_B(reg_ab_1_out_b));
  IReg ireg_2 (.LE(DI), .In(eeprom_1_data), .Out(ireg_2_out));
  FlipFlop flipflop_2 (.toggle(button_2_out), .Q(flipflop_2_q));
  // Probe on pc_1_debug_out
  // Probe on ireg_2_out
  // Probe on ireg_2_out
  Button button_2 (.out(button_2_out));

  // Notes on the sheet:
  //   Clock Halt Manual
endmodule

// Reg
module Reg_AB (
  input  LE_A,
  input  NOT_EOA,
  input  LE_B,
  input  NOT_OEB,
  input  [7:0] In,
  output [7:0] A_E,
  output [7:0] Out_A,
  output [7:0] B_E,
  output [7:0] Out_B
);

  wire [7:0] bustranscever_1_a, bustranscever_1_b, bustranscever_2_a, bustranscever_2_b;

  DIP_74574 dip_74574_1 (
    .Q1(Out_A[0]), .Q2(Out_A[1]), .Q3(Out_A[2]), .Q4(Out_A[3]), .Q5(Out_A[4]), .Q6(Out_A[5]), .Q7(Out_A[6]),
    .Q8(Out_A[7]), .D1(In[0]), .D2(In[1]), .OE(1'b0), .D3(In[2]), .D4(In[3]), .D5(In[4]), .D6(In[5]),
    .D7(In[6]), .CLK(LE_A), .D8(In[7]));
  DIP_74574 dip_74574_2 (
    .Q1(Out_B[0]), .Q2(Out_B[1]), .Q3(Out_B[2]), .Q4(Out_B[3]), .Q5(Out_B[4]), .Q6(Out_B[5]), .Q7(Out_B[6]),
    .Q8(Out_B[7]), .D1(In[0]), .D2(In[1]), .OE(1'b0), .D3(In[2]), .D4(In[3]), .D5(In[4]), .D6(In[5]),
    .D7(In[6]), .CLK(LE_B), .D8(In[7]));
  BusTranscever bustranscever_1 (
    .Ain(bustranscever_1_a), .Bin(bustranscever_1_b), .dir(1'b1), .NOT_OE(NOT_EOA), .A(bustranscever_1_a),
    .B(bustranscever_1_b));
  BusTranscever bustranscever_2 (
    .Ain(bustranscever_2_a), .Bin(bustranscever_2_b), .dir(1'b1), .NOT_OE(NOT_OEB), .A(bustranscever_2_a),
    .B(bustranscever_2_b));

  // Other names for the same wires on the sheet: NOT_EOB = NOT_OEB
endmodule

module Display (
  input  [7:0] in_1
);

  Hex_Digit_Display hex_digit_display_1 (.value(in_1[3:0]), .dp(1'b0));
  Hex_Digit_Display hex_digit_display_2 (.value(in_1[7:4]), .dp(1'b0));
endmodule

module Clock (
  input  ClkHalt,
  input  ClkMan,
  output Clk
);

  wire and_1_out, clock_1_out, not_1_out;

  Clock_part clock_1 (.out(clock_1_out));
  and and_1 (and_1_out, clock_1_out, not_1_out);
  not not_1 (not_1_out, ClkHalt);
  or or_1 (Clk, and_1_out, ClkMan);
endmodule

module PC (
  input  Clk,
  input  NOT_load,
  input  NOT_OE,
  input  PC_INC,
  input  [7:0] LoadIn,
  output [7:0] Debug_Out,
  output [7:0] PCout
);

  wire dip_74163_1_tc;

  LED IN_LED (.in(NOT_load));
  LED OUT_LED (.in(NOT_OE));
  DIP_74163 dip_74163_1 (
    .Q1(Debug_Out[0]), .Q2(Debug_Out[1]), .Q3(Debug_Out[2]), .Q4(Debug_Out[3]), .TC(dip_74163_1_tc),
    .LE(NOT_load), .CEP(PC_INC), .CET(PC_INC), .CLK(Clk), .D1(LoadIn[0]), .D2(LoadIn[1]), .D3(LoadIn[2]),
    .CE(1'b0), .D4(LoadIn[3]));
  DIP_74163 dip_74163_2 (
    .Q1(Debug_Out[4]), .Q2(Debug_Out[5]), .Q3(Debug_Out[6]), .Q4(Debug_Out[7]), .LE(NOT_load),
    .CEP(dip_74163_1_tc), .CET(dip_74163_1_tc), .CLK(Clk), .D1(LoadIn[4]), .D2(LoadIn[5]), .D3(LoadIn[6]),
    .CE(1'b0), .D4(LoadIn[7]));  // open: TC
  BusTranscever bustranscever_1 (.Ain(Debug_Out), .Bin(PCout), .dir(1'b0), .NOT_OE(NOT_OE), .A(Debug_Out), .B(PCout));

  // Other names for the same wires on the sheet: INC = PC_INC; NOT_EO = NOT_OE

  // Notes on the sheet:
  //   74163: https://www.ti.com/lit/ds/symlink/sn54ls161a.pdf?ts=1736241297246&ref_url=https%253A%252F%252Fwww.google.com%252F
endmodule

module RAM (
  input  LoadAdr,
  input  NOT_EO,
  input  NOT_write,
  input  [7:0] adr,
  input  [7:0] Din,
  output [7:0] Dout
);

  wire EO, write;
  wire [7:0] bustranscever_1_a, bustranscever_1_b, dip_74574_1_q1, ram_1_dout;

  not not_1 (write, NOT_write);
  DIP_74574 dip_74574_1 (
    .Q1(dip_74574_1_q1[0]), .Q2(dip_74574_1_q1[1]), .Q3(dip_74574_1_q1[2]), .Q4(dip_74574_1_q1[3]),
    .Q5(dip_74574_1_q1[4]), .Q6(dip_74574_1_q1[5]), .Q7(dip_74574_1_q1[6]), .Q8(dip_74574_1_q1[7]),
    .D1(adr[0]), .D2(adr[1]), .OE(1'b0), .D3(adr[2]), .D4(adr[3]), .D5(adr[4]), .D6(adr[5]), .D7(adr[6]),
    .CLK(LoadAdr), .D8(adr[7]));
  not not_2 (EO, NOT_EO);
  RAM_part #(.trigger("high"), .\type ("nonvolatile")) ram_1 (
    .addr(dip_74574_1_q1), .we(write), .oe(EO), .din(Din), .dout(ram_1_dout));
  BusTranscever bustranscever_1 (
    .Ain(bustranscever_1_a), .Bin(bustranscever_1_b), .dir(1'b0), .NOT_OE(NOT_EO), .A(bustranscever_1_a),
    .B(bustranscever_1_b));

  // Other names for the same wires on the sheet: LE = LoadAdr; NEO = NOT_EO
endmodule

module EEPROM (
  input  LoadAdr,
  input  NOT_EO,
  input  NOT_write,
  input  args,
  input  [7:0] adr,
  input  [7:0] in,
  output [7:0] data
);

  wire EO, write;
  wire [7:0] bustranscever_1_a, bustranscever_1_b, dip_74574_1_q1, ram_1_dout;

  not not_1 (write, NOT_write);
  DIP_74574 dip_74574_1 (
    .Q1(dip_74574_1_q1[0]), .Q2(dip_74574_1_q1[1]), .Q3(dip_74574_1_q1[2]), .Q4(dip_74574_1_q1[3]),
    .Q5(dip_74574_1_q1[4]), .Q6(dip_74574_1_q1[5]), .Q7(dip_74574_1_q1[6]), .Q8(dip_74574_1_q1[7]),
    .D1(adr[0]), .D2(adr[1]), .OE(1'b0), .D3(adr[2]), .D4(adr[3]), .D5(adr[4]), .D6(adr[5]), .D7(adr[6]),
    .CLK(LoadAdr), .D8(adr[7]));
  not not_2 (EO, NOT_EO);
  RAM_part #(.addrWidth(9), .trigger("high"), .\type ("nonvolatile")) ram_1 (
    .addr({args, dip_74574_1_q1}), .we(write), .oe(EO), .din(in), .dout(ram_1_dout));
  BusTranscever bustranscever_1 (
    .Ain(bustranscever_1_a), .Bin(bustranscever_1_b), .dir(1'b0), .NOT_OE(NOT_EO), .A(bustranscever_1_a),
    .B(bustranscever_1_b));

  // Other names for the same wires on the sheet: LE = LoadAdr; NEO = NOT_EO

  // Notes on the sheet:
  //   Args, der 2te speicherbereich für die Argumente der Befehle im ersten Speicherbereich
  //   Argument soll auf lsb, damit es hinter der Instruction steht
endmodule

module ALU (
  input  Binv,
  input  [7:0] A,
  input  Cin,
  input  [7:0] B,
  output [7:0] Y,
  output Cout
);

  wire B0, B1, B2, B3, B4, B5, B6, B7, Carry;

  mdip_74283 mdip_74283_1 (
    .B1(B0), .A2(B1), .CIN(Cin), .B2(A[1]), .A3(A[2]), .B3(B2), .A4(B3), .B4(A[3]), .A1(A[0]), .Y2(Y[1]),
    .Y3(Y[2]), .Y1(Y[0]), .Y4(Y[3]), .COUT(Carry));
  mdip_74283 mdip_74283_2 (
    .B1(B4), .A2(B5), .CIN(Carry), .B2(A[5]), .A3(A[6]), .B3(B6), .A4(B7), .B4(A[7]), .A1(A[4]), .Y2(Y[5]),
    .Y3(Y[6]), .Y1(Y[4]), .Y4(Y[7]), .COUT(Cout));
  DIP_7486 dip_7486_1 (
    .Y2(B1), .Y3(B2), .Y4(B3), .Y1(B0), .A2(Binv), .B2(B[1]), .A3(Binv), .A1(Binv), .B3(B[2]), .A4(Binv),
    .B4(B[3]), .B1(B[0]));
  DIP_7486 dip_7486_2 (
    .Y2(B5), .Y3(B6), .Y4(B7), .Y1(B4), .A2(Binv), .B2(B[5]), .A3(Binv), .A1(Binv), .B3(B[6]), .A4(Binv),
    .B4(B[7]), .B1(B[4]));

  // Other names for the same wires on the sheet: rB0 = B[0]; rB1 = B[1]; rB2 = B[2]; rB3 = B[3]; rB4 = B[4];
  //   rB5 = B[5]; rB6 = B[6]; rB7 = B[7]
endmodule

// 74LS245
module L_74_245_4198fcca (
  input  Dir,
  input  NOT_OE_5a23fa50,
  input  A1,
  input  in_4,
  input  in_5,
  input  in_6,
  input  A3,
  input  B3,
  input  A4,
  input  B4,
  input  A5,
  input  B5,
  input  in_13,
  input  B6,
  input  A7,
  input  B7,
  input  in_17,
  input  B8,
  output B1,
  output out_20,
  output B2,
  output A2,
  output out_23,
  output out_24,
  output out_25,
  output out_26,
  output out_27,
  output out_28,
  output out_29,
  output A6,
  output out_31,
  output out_32,
  output out_33,
  output A8
);

  wire and_1_out, and_2_out;

  and and_1 (and_1_out, Dir, ~NOT_OE_5a23fa50);  // AND_Gate
  assign B1 = and_1_out ? A1 : 1'bz;  // Controlled_Buffer controlled_buffer_1
  assign B2 = and_1_out ? in_5 : 1'bz;  // Controlled_Buffer controlled_buffer_2
  assign out_23 = and_1_out ? A3 : 1'bz;  // Controlled_Buffer controlled_buffer_3
  assign out_25 = and_1_out ? A4 : 1'bz;  // Controlled_Buffer controlled_buffer_4
  assign out_27 = and_1_out ? A5 : 1'bz;  // Controlled_Buffer controlled_buffer_5
  assign out_29 = and_1_out ? in_13 : 1'bz;  // Controlled_Buffer controlled_buffer_6
  assign out_31 = and_1_out ? A7 : 1'bz;  // Controlled_Buffer controlled_buffer_7
  assign out_33 = and_1_out ? in_17 : 1'bz;  // Controlled_Buffer controlled_buffer_8
  and and_2 (and_2_out, ~Dir, ~NOT_OE_5a23fa50);  // AND_Gate
  assign out_20 = and_2_out ? in_4 : 1'bz;  // Controlled_Buffer controlled_buffer_9
  assign A2 = and_2_out ? in_6 : 1'bz;  // Controlled_Buffer controlled_buffer_10
  assign out_24 = and_2_out ? B3 : 1'bz;  // Controlled_Buffer controlled_buffer_11
  assign out_26 = and_2_out ? B4 : 1'bz;  // Controlled_Buffer controlled_buffer_12
  assign out_28 = and_2_out ? B5 : 1'bz;  // Controlled_Buffer controlled_buffer_13
  assign A6 = and_2_out ? B6 : 1'bz;  // Controlled_Buffer controlled_buffer_14
  assign out_32 = and_2_out ? B7 : 1'bz;  // Controlled_Buffer controlled_buffer_15
  assign A8 = and_2_out ? B8 : 1'bz;  // Controlled_Buffer controlled_buffer_16
endmodule

// 245_BT
module BusTranscever (
  input  NOT_OE,
  input  dir,
  input  [7:0] Ain,
  input  [7:0] Bin,
  output [7:0] A,
  output [7:0] B
);

  wire DIR_AND_NOE, NDIR_AND_NOE, NOT_dir, OE;
  wire [7:0] controlled_buffer_1_out, l_74_245_4198fcca_1_b1;

  not not_1 (OE, NOT_OE);
  not not_2 (NOT_dir, dir);
  assign controlled_buffer_1_out = dir ? Ain : 8'bz;  // Controlled_Buffer controlled_buffer_1
  assign A = DIR_AND_NOE ? controlled_buffer_1_out : 8'bz;  // Controlled_Buffer controlled_buffer_2
  L_74_245_4198fcca l_74_245_4198fcca_1 (
    .Dir(dir), .A1(controlled_buffer_1_out[0]), .in_5(controlled_buffer_1_out[1]),
    .A3(controlled_buffer_1_out[2]), .A4(controlled_buffer_1_out[3]), .A5(controlled_buffer_1_out[4]),
    .in_13(controlled_buffer_1_out[5]), .A7(controlled_buffer_1_out[6]), .in_17(controlled_buffer_1_out[7]),
    .NOT_OE_5a23fa50(NOT_OE), .in_4(l_74_245_4198fcca_1_b1[0]), .in_6(l_74_245_4198fcca_1_b1[1]),
    .B3(l_74_245_4198fcca_1_b1[2]), .B4(l_74_245_4198fcca_1_b1[3]), .B5(l_74_245_4198fcca_1_b1[4]),
    .B6(l_74_245_4198fcca_1_b1[5]), .B7(l_74_245_4198fcca_1_b1[6]), .B8(l_74_245_4198fcca_1_b1[7]),
    .out_20(controlled_buffer_1_out[0]), .A2(controlled_buffer_1_out[1]),
    .out_24(controlled_buffer_1_out[2]), .out_26(controlled_buffer_1_out[3]),
    .out_28(controlled_buffer_1_out[4]), .A6(controlled_buffer_1_out[5]),
    .out_32(controlled_buffer_1_out[6]), .A8(controlled_buffer_1_out[7]), .B1(l_74_245_4198fcca_1_b1[0]),
    .B2(l_74_245_4198fcca_1_b1[1]), .out_23(l_74_245_4198fcca_1_b1[2]), .out_25(l_74_245_4198fcca_1_b1[3]),
    .out_27(l_74_245_4198fcca_1_b1[4]), .out_29(l_74_245_4198fcca_1_b1[5]),
    .out_31(l_74_245_4198fcca_1_b1[6]), .out_33(l_74_245_4198fcca_1_b1[7]));
  assign l_74_245_4198fcca_1_b1 = NOT_dir ? Bin : 8'bz;  // Controlled_Buffer controlled_buffer_3
  and and_1 (NDIR_AND_NOE, OE, dir);
  and and_2 (DIR_AND_NOE, OE, NOT_dir);
  assign B = NDIR_AND_NOE ? l_74_245_4198fcca_1_b1 : 8'bz;  // Controlled_Buffer controlled_buffer_4
endmodule

// ALU
module ALU_T_a1d61d21 (
  input  NOT_EO_36d354d6,
  input  Cin,
  input  Binv,
  input  [7:0] A,
  input  [7:0] B,
  output [7:0] out,
  output Zero
);

  wire dip_7402_1_y1, dip_7402_1_y2, dip_7402_1_y3, dip_7402_1_y4, dip_7408_1_y1, dip_7408_1_y4;
  wire [7:0] alu_1_y, bustranscever_1_a, bustranscever_1_b;

  BusTranscever bustranscever_1 (
    .Ain(bustranscever_1_a), .Bin(bustranscever_1_b), .dir(1'b0), .NOT_OE(NOT_EO_36d354d6),
    .A(bustranscever_1_a), .B(bustranscever_1_b));
  ALU alu_1 (.A(A), .Binv(Binv), .Cin(Cin), .B(B), .Y(alu_1_y));  // open: Cout
  DIP_7402 dip_7402_1 (
    .Y2(dip_7402_1_y2), .Y3(dip_7402_1_y3), .Y4(dip_7402_1_y4), .Y1(dip_7402_1_y1), .A2(alu_1_y[3]),
    .B2(alu_1_y[2]), .A3(alu_1_y[4]), .A1(alu_1_y[0]), .B3(alu_1_y[5]), .A4(alu_1_y[6]), .B4(alu_1_y[7]),
    .B1(alu_1_y[1]));
  DIP_7408 dip_7408_1 (
    .Y2(Zero), .Y4(dip_7408_1_y4), .Y1(dip_7408_1_y1), .A2(dip_7408_1_y1), .B2(dip_7408_1_y4),
    .A1(dip_7402_1_y4), .A4(dip_7402_1_y2), .B4(dip_7402_1_y1), .B1(dip_7402_1_y3));  // open: Y3, A3, B3
endmodule

// T-FF
module FlipFlop (
  input  toggle,
  output Q
);

  J_K_Flip_Flop j_k_ff_1 (.J(toggle), .K(toggle), .clk(toggle), .Q(Q));  // open: Qn, preset, reset
endmodule

module InstReg (
  input  NOT_OE_5a23fa50,
  input  LE,
  input  [7:0] In,
  output [7:0] Out_A_d614a9c4
);

  DIP_74574 dip_74574_1 (
    .Q1(Out_A_d614a9c4[0]), .Q2(Out_A_d614a9c4[1]), .Q3(Out_A_d614a9c4[2]), .Q4(Out_A_d614a9c4[3]),
    .Q5(Out_A_d614a9c4[4]), .Q6(Out_A_d614a9c4[5]), .Q7(Out_A_d614a9c4[6]), .Q8(Out_A_d614a9c4[7]),
    .D1(In[0]), .D2(In[1]), .OE(NOT_OE_5a23fa50), .D3(In[2]), .D4(In[3]), .D5(In[4]), .D6(In[5]), .D7(In[6]),
    .CLK(LE), .D8(In[7]));
endmodule

// IREG
module IReg (
  input  LE,
  input  [7:0] In,
  output [7:0] Out
);

  DIP_74574 dip_74574_1 (
    .Q1(Out[0]), .Q2(Out[1]), .Q3(Out[2]), .Q4(Out[3]), .Q5(Out[4]), .Q6(Out[5]), .Q7(Out[6]), .Q8(Out[7]),
    .D1(In[0]), .D2(In[1]), .OE(1'b0), .D3(In[2]), .D4(In[3]), .D5(In[4]), .D6(In[5]), .D7(In[6]), .CLK(LE),
    .D8(In[7]));

  // Notes on the sheet:
  //   Durchlässiger 573er für register unbrauchbar, muss 574 sein, getakted
endmodule

// Instruction Logic
module ControllLogic (
  input  zero,
  input  Clk,
  input  [7:0] IREG,
  input  halt_man,
  output PC_LOAD_I,
  output RAM_ADR_I,
  output EEPROM_ADR_I,
  output REG_A_I,
  output REG_B_I,
  output REG_INST_I,
  output RAM_WRITE_I,
  output PC_O,
  output EEPROM_WRITE_I,
  output RAM_O,
  output EEPROM_O,
  output REG_A_O,
  output REG_B_O,
  output ALU_O,
  output halt,
  output out_20,
  output out_21,
  output PC_INC,
  output ALU_Cin,
  output ALU_Binv,
  output EEPROM_ARG,
  output Disp_I
);

  wire dip_7408_2_y2, dip_74138_1_y1, dip_74138_1_y2, dip_74138_1_y3, dip_74138_1_y4, dip_74138_1_y5,
       dispI_I, EEPAI_I, EEPWI_I, halt_soft, JUMP_I2, not_6_out, not_7_out, PCLI_I, RAMAI_I, RAMWI_I,
       REGAI_I, REGBI_I, REGII_I;
  wire [3:0] I_MEM_ADD;
  wire [7:0] H_Inst;
  wire [7:4] IndipendentSig;

  DIP_74163 dip_74163_1 (
    .Q1(I_MEM_ADD[0]), .Q2(I_MEM_ADD[1]), .Q3(I_MEM_ADD[2]), .Q4(I_MEM_ADD[3]), .LE(1'b1), .CEP(1'b1),
    .CET(1'b1), .CLK(Clk), .D1(1'b0), .D2(1'b0), .D3(1'b0), .CE(IndipendentSig[7]), .D4(1'b0));  // open: TC
  DIP_74138 dip_74138_1 (
    .Y0(PCLI_I), .Y1(dip_74138_1_y1), .Y2(dip_74138_1_y2), .Y3(dip_74138_1_y3), .Y4(dip_74138_1_y4),
    .Y5(dip_74138_1_y5), .Y6(RAMWI_I), .Y7(EEPWI_I), .A0(H_Inst[4]), .A1(H_Inst[5]), .OE1(1'b0), .in_5(1'b0),
    .OE2(H_Inst[7]), .A2(H_Inst[6]));
  DIP_74138 dip_74138_2 (
    .Y0(PC_O), .Y1(RAM_O), .Y2(EEPROM_O), .Y3(REG_A_O), .Y4(REG_B_O), .Y5(ALU_O), .Y6(out_20), .Y7(out_21),
    .A0(H_Inst[0]), .A1(H_Inst[1]), .OE1(1'b0), .in_5(1'b0), .OE2(H_Inst[3]), .A2(H_Inst[2]));
  not not_1 (RAMAI_I, dip_74138_1_y1);
  not not_2 (EEPAI_I, dip_74138_1_y2);
  not not_3 (REGAI_I, dip_74138_1_y3);
  not not_4 (REGBI_I, dip_74138_1_y4);
  not not_5 (REGII_I, dip_74138_1_y5);
  ROM #(.addrWidth(12)) rom_1 (.addr({IREG, I_MEM_ADD}), .data(H_Inst));
  not not_6 (not_6_out, JUMP_I2);
  DIP_7408 dip_7408_1 (
    .Y2(EEPROM_ADR_I), .Y3(REG_B_I), .Y4(REG_A_I), .Y1(RAM_ADR_I), .A2(Clk), .B2(EEPAI_I), .A3(Clk),
    .A1(Clk), .B3(REGBI_I), .A4(REGAI_I), .B4(Clk), .B1(RAMAI_I));
  DIP_7408 dip_7408_2 (
    .Y2(dip_7408_2_y2), .Y3(JUMP_I2), .Y4(Disp_I), .Y1(REG_INST_I), .A2(PCLI_I), .B2(not_6_out), .A3(zero),
    .A1(Clk), .B3(IndipendentSig[4]), .A4(dispI_I), .B4(Clk), .B1(REGII_I));
  not not_7 (not_7_out, Clk);
  DIP_7432 dip_7432_1 (
    .Y2(RAM_WRITE_I), .Y3(halt), .Y4(EEPROM_WRITE_I), .Y1(PC_LOAD_I), .A2(not_7_out), .B2(RAMWI_I),
    .A3(halt_soft), .A1(not_7_out), .B3(halt_man), .A4(EEPWI_I), .B4(not_7_out), .B1(dip_7408_2_y2));
  ROM #(.addrWidth(12)) rom_2 (
    .addr({IREG, I_MEM_ADD}),
    .data({IndipendentSig[7], halt_soft, dispI_I, IndipendentSig[4], EEPROM_ARG, ALU_Binv, ALU_Cin, PC_INC}));

  // Other names for the same wires on the sheet: EEPAI = EEPROM_ADR_I; EEPWI = EEPROM_WRITE_I; out_Enable = H_Inst[3];
  //   in_Enable = H_Inst[7]; Istep[3:0] = I_MEM_ADD; I_MEM_ADD[11:4] = IREG; Iadr[7:0] = IREG;
  //   IndipendentSig (some bits) = {halt_soft, dispI_I, EEPROM_ARG, ALU_Binv, ALU_Cin, PC_INC};
  //   L_Inst[7:0] = {IndipendentSig[7], halt_soft, dispI_I, IndipendentSig[4], EEPROM_ARG, ALU_Binv, ALU_Cin, PC_INC};
  //   jump_I = IndipendentSig[4]; stepReset = IndipendentSig[7]; inSignalsDec[2:0] = H_Inst[6:4];
  //   outSignalsDec[2:0] = H_Inst[2:0]; PCLI = PC_LOAD_I; RAMAI = RAM_ADR_I; RAMWI = RAM_WRITE_I; REGAI = REG_A_I;
  //   REGBI = REG_B_I; REGII = REG_INST_I

  // Notes on the sheet:
  //   OUTPUT
  //   Noch Zwei Outputs Frei zum Anbringen
  //   Eingabe vllt ?
  //   contents of rom_1 (hex, n*v repeats v):
  //   a8 da 14*0 a8 da 9a ed 12*0 a8 da 9a ed 12*0 a8 da 9a b9 12*0 a8 da 9a c9 12*0 a8 da 8a 13*0 a8 da
  //   9a 9 12*0 a8 da 9a 13*0 a8 da ea 13*0 a8 da 9a 9 12*0 a8 da
  //   IO Rom
  //   Clock, für synchrones laden der Werte
  //   not_Jmp
  //   Clock Halt
  //   Führt zu PCLI
  //   contents of rom_2 (hex, n*v repeats v):
  //   0 0 81 15*0 8 0 81 13*0 8 6 81 13*0 8 0 81 13*0 8 0 81 13*0 8 81 14*0 8 10 81 13*0 8 81 14*0 8 81
  //   14*0 8 20 81 13*0 40 81
  //   1
  //   2
  //   4
  //   Special Instruction Rom
  //   8
  //   10
  //   80
  //   20
  //   INPUT
  //   NC zu Clock Halt
  //   40
endmodule

// 74283
module mdip_74283 (
  input  CIN,
  input  A1,
  input  B1,
  input  A2,
  input  B2,
  input  A3,
  input  B3,
  input  A4,
  input  B4,
  output Y1,
  output Y2,
  output Y3,
  output Y4,
  output COUT
);

  wire and_1_out, and_2_out, and_3_out, and_4_out, and_5_out, and_6_out, and_7_out, and_8_out, and_9_out,
       and_10_out, and_11_out, and_12_out, and_13_out, and_14_out, nand_1_out, nand_2_out, nand_3_out,
       nand_4_out, nor_1_out, nor_2_out, nor_3_out, nor_4_out, nor_5_out, nor_6_out, nor_7_out, not_1_out,
       not_2_out, not_3_out, not_4_out, not_5_out, not_6_out;

  not not_1 (not_1_out, CIN);
  nor nor_1 (nor_1_out, A1, B1);
  nand nand_1 (nand_1_out, A1, B1);
  nor nor_2 (nor_2_out, A2, B2);
  nand nand_2 (nand_2_out, A2, B2);
  nor nor_3 (nor_3_out, A3, B3);
  nand nand_3 (nand_3_out, A3, B3);
  nor nor_4 (nor_4_out, A4, B4);
  nand nand_4 (nand_4_out, A4, B4);
  not not_2 (not_2_out, not_1_out);
  not not_3 (not_3_out, nor_1_out);
  and and_1 (and_1_out, not_1_out, nand_1_out);
  not not_4 (not_4_out, nor_2_out);
  and and_2 (and_2_out, not_1_out, nand_1_out, nand_2_out);
  and and_3 (and_3_out, nand_2_out, nor_1_out);
  not not_5 (not_5_out, nor_3_out);
  and and_4 (and_4_out, not_1_out, nand_1_out, nand_2_out, nand_3_out);
  and and_5 (and_5_out, nand_2_out, nand_3_out, nor_1_out);
  and and_6 (and_6_out, nand_3_out, nor_2_out);
  not not_6 (not_6_out, nor_4_out);
  and and_7 (and_7_out, not_1_out, nand_1_out, nand_2_out, nand_3_out, nand_4_out);
  and and_8 (and_8_out, nand_2_out, nand_3_out, nand_4_out, nor_1_out);
  and and_9 (and_9_out, nand_3_out, nand_4_out, nor_2_out);
  and and_10 (and_10_out, nand_4_out, nor_3_out);
  and and_11 (and_11_out, not_3_out, nand_1_out);
  nor nor_5 (nor_5_out, and_1_out, nor_1_out);
  and and_12 (and_12_out, not_4_out, nand_2_out);
  nor nor_6 (nor_6_out, and_2_out, and_3_out, nor_2_out);
  and and_13 (and_13_out, not_5_out, nand_3_out);
  nor nor_7 (nor_7_out, and_4_out, and_5_out, and_6_out, nor_3_out);
  and and_14 (and_14_out, not_6_out, nand_4_out);
  nor nor_8 (COUT, and_7_out, and_8_out, and_9_out, and_10_out, nor_4_out);
  xor xor_1 (Y1, not_2_out, and_11_out);
  xor xor_2 (Y2, nor_5_out, and_12_out);
  xor xor_3 (Y3, nor_6_out, and_13_out);
  xor xor_4 (Y4, nor_7_out, and_14_out);
endmodule
